// Logisim project RoadRipper.circ as structural Verilog: 2 circuits, main circuit main
module main (
  input  Stop,
  input  Left,
  input  Right,
  input  Clock,
  output R_Back,
  output R_Front,
  output L_Back,
  output L_Front
);
endmodule

module RR_MUX_version (
  input  Stop,
  input  Left,
  input  Right,
  input  Clock,
  output L_Front,
  output L_Back,
  output R_Front,
  output R_Back
);

  Multiplexer #(.select(4), .enable("false")) multiplexer_1 (
    .in0(1'b0), .in1(1'b0), .in2(1'b0), .in3(1'b0), .in4(1'b0), .in5(1'b1), .in6(1'b0), .in7(1'b1),
    .in8(1'b0), .in9(1'b0), .in10(1'b0), .in11(1'b0), .in12(1'b0), .in13(1'b1), .in14(1'b0), .in15(1'b1),
    .out(L_Front), .sel({Stop, Left, Right, Clock}));
  // Probe on {Stop, Left, Right, Clock}
  Multiplexer #(.select(4), .enable("false")) multiplexer_2 (
    .out(L_Back), .sel({Stop, Left, Right, Clock}));  // open: in0, in1, in2, in3, in4, in5, in6, in7, in8, in9, in10, in11, in12, in13, in14, in15
  Multiplexer #(.select(4), .enable("false")) multiplexer_3 (
    .out(R_Front), .sel({Stop, Left, Right, Clock}));  // open: in0, in1, in2, in3, in4, in5, in6, in7, in8, in9, in10, in11, in12, in13, in14, in15
  Multiplexer #(.select(4), .enable("false")) multiplexer_4 (
    .out(R_Back), .sel({Stop, Left, Right, Clock}));  // open: in0, in1, in2, in3, in4, in5, in6, in7, in8, in9, in10, in11, in12, in13, in14, in15
endmodule
