// Logisim project Register_File.circ as structural Verilog: 2 circuits, main circuit main
module main (
  input  WE,
  input  [2:0] WAddr,
  input  Data_in,
  input  Clk,
  input  [3:0] RAddr,
  output [3:0] Data_out
);

  Decoder #(.select(3)) decoder_1 ();  // open: out0, out1, out2, out3, out4, out5, out6, out7, sel, en
  Four_bit_register four_bit_register_1 ();  // open: Din, Write, Clk, Dout
  Four_bit_register four_bit_register_2 ();  // open: Din, Write, Clk, Dout
  Four_bit_register four_bit_register_3 ();  // open: Din, Write, Clk, Dout
  Four_bit_register four_bit_register_4 ();  // open: Din, Write, Clk, Dout
  Four_bit_register four_bit_register_5 ();  // open: Din, Write, Clk, Dout
  Four_bit_register four_bit_register_6 ();  // open: Din, Write, Clk, Dout
  Four_bit_register four_bit_register_7 ();  // open: Din, Write, Clk, Dout
  Four_bit_register four_bit_register_8 ();  // open: Din, Write, Clk, Dout
  Multiplexer #(.select(3), .width(4), .enable("false")) multiplexer_1 (.out(Data_out));  // open: in0, in1, in2, in3, in4, in5, in6, in7, sel
endmodule

module Four_bit_register (
  input  [3:0] Din,
  input  Write,
  input  Clk,
  output [3:0] Dout
);
endmodule
